# Fritzing sketch Diagram (saved by Fritzing 0.9.3b)
breadboards: 1

parts:
  Part1 = Arduino Uno (Rev3)
  LED_Correct = LED - 5mm [color="Red (633nm)" package="5 mm [THT]"]
  LED_Bad = LED - 5mm [color="Red (633nm)" package="5 mm [THT]"]
  Matrix_keypad = KEYPAD 4x4
  PNP = NPN-Transistor [package="TO92 [THT]"]
  Relay = RELAY [package=relay-g5q]
  Power_12V = Power plug
  Solenoid = Solenoid

nets:
  N1: Part1.D8, Matrix_keypad.row3
  N2: Part1.D9_PWM, Matrix_keypad.row4
  N3: Part1.D10_PWM/SS, LED_Correct.anode
  N4: Part1.D11_PWM/MOSI, PNP.B
  N5: Part1.D12/MISO, LED_Bad.anode
  N6: Part1.GND, PNP.C
  N7: Part1.D2, Matrix_keypad.col1
  N8: Part1.D3_PWM, Matrix_keypad.col2
  N9: Part1.D4, Matrix_keypad.col3
  N10: Part1.D5_PWM, Matrix_keypad.col4
  N11: Part1.D6_PWM, Matrix_keypad.row1
  N12: Part1.D7, Matrix_keypad.row2
  N13: Part1.5V, LED_Correct.cathode, LED_Bad.cathode, Relay.COIL2
  N14: PNP.E, Relay.COIL1
  N15: Relay.MAIN, Power_12V.GND
  N16: Relay.NO, Solenoid.pin1
  N17: Power_12V.VCC, Solenoid.pin2

custom parts:
  KEYPAD 4x4: Matrix keypad 16 buttons, 4 rows x 4 columns

// code stored in the sketch: Security-Room.ino
#include <Keypad.h>

#define ledPin 12
#define ledPinR 10
#define signalPin 11

#define Password_Length 10

char Data[Password_Length]; 
char Master[Password_Length] = "241997"; 
byte data_count = 0, master_count = 0;
bool Pass_is_good;

const byte ROWS = 4; 
const byte COLS = 4; 
  
char hexaKeys[ROWS][COLS] = {
  {'1', '2', '3', 'A'},
  {'4', '5', '6', 'B'},
  {'7', '8', '9', 'C'},
  {'*', '0', '#', 'D'}
};

byte rowPins[ROWS] = {9, 8, 7, 6}; 
byte colPins[COLS] = {5, 4, 3, 2}; 

Keypad cKeypad = Keypad(makeKeymap(hexaKeys), rowPins, colPins, ROWS, COLS); 

void setup(){
  Serial.begin(9600);
  digitalWrite(ledPin, HIGH);   // sets the LED on
  pinMode(ledPinR, OUTPUT);      // sets the digital pin as output
  pinMode(signalPin, OUTPUT);  // sets the digital pin as output relay
  Serial.println("Enter password:");
  cKeypad.addEventListener(keypadEvent); //add an event listener for this keypad
}
  
void loop(){
  char customKey = cKeypad.getKey();
  if (customKey){
    if (customKey != '*') {
      Data[data_count] = customKey; 
      data_count++;
      //Serial.println(customKey);
    }
  }
}

//take care of some special events
void keypadEvent(KeypadEvent eKey){
  switch (eKey){
    case '*': 
    Serial.println("Checking...");
    guessPassword(); 
    break;
    case '#': 
    Serial.println("Cleaning...");
    clearData();
    delay(100);
    break;
  }
}

//function to check allright password
void guessPassword(){
  Serial.print(Data);
  if (!strcmp(Data, Master)){
    Serial.println("OK");
    digitalWrite(ledPin, LOW); //led indicator on green
    digitalWrite(signalPin, HIGH); //Relay pin
    delay(500);//delay for wait a 6s before deleting a prev password
    digitalWrite(signalPin, LOW); //Relay pin
    digitalWrite(ledPin, HIGH); //led indicator green
    //digitalWrite(ledPinR, LOW); //led indicator red    
    delay(1000);
    clearData(); //Clean data array  
  } else {
    Serial.println("Incorrect");
    clearData();
  }
}
void clearData(){
  digitalWrite(ledPinR, HIGH); //led indicator red
  digitalWrite(ledPin, LOW); //led indicator green
  delay(500);
  digitalWrite(ledPinR, LOW); //led indicator red
  digitalWrite(ledPin, HIGH); //led indicator green  
  while(data_count != 0){
    Data[data_count--] = 0; 
  }
  return;
}
